// Logisim project seven-segment-name-display.circ as structural Verilog: 1 circuit, main circuit main
module main (
);

  wire _0_out, A_2_out, A_3_out, a_4_out, A_out, b_out, c_out, D_2_out, d_3_out, D_out, E_2_out, e_3_out,
       E_out, f_out, g_2_out, G_out, I_out, M_2_out, M_out, N_out, not_1_out, not_2_out, not_3_out,
       not_4_out, not_5_out, not_6_out, not_7_out, not_8_out, not_9_out, not_10_out, not_11_out, not_12_out,
       not_13_out, not_14_out, not_15_out, not_16_out, not_17_out, R_out, t_prime_y_z_out,
       t_prime_z_prime_out, t_x_y_out, x_prime_yz_out, x_prime_yz_prime_t_prime_out, x_prime_zt_prime_out,
       x_y__prime_out, x_y_out, x_y_t__prime_out, xy_prime_zt_out, xy_t_prime_z_prime_out, xyt_out, xz_out,
       xz_prime_out, xz_prime_t_prime_out, y_prime_t_out, y_prime_zt_prime_out, y_t__prime_out, y_t_out,
       y_z_out, yt_prime_out, Z_2_out, Z_out, z_prime_t_out, z_prime_x_y_out, zt_prime_x_y__prime_out;
  wire [3:0] priority_encoder_1_out;

  Button _0 (.out(_0_out));
  Button N (.out(N_out));
  Button A (.out(A_out));
  Button R (.out(R_out));
  Button G (.out(G_out));
  Button I (.out(I_out));
  Button Z (.out(Z_out));
  Button M (.out(M_out));
  Button A_2 (.out(A_2_out));
  Button M_2 (.out(M_2_out));
  Button E (.out(E_out));
  Button D (.out(D_out));
  Button Z_2 (.out(Z_2_out));
  Button A_3 (.out(A_3_out));
  Button D_2 (.out(D_2_out));
  Button E_2 (.out(E_2_out));
  Priority_Encoder #(.select(4), .disabled(0)) priority_encoder_1 (
    .in0(_0_out), .in1(N_out), .in2(A_out), .in3(R_out), .in4(G_out), .in5(I_out), .in6(Z_out), .in7(M_out),
    .in8(A_2_out), .in9(M_2_out), .in10(E_out), .in11(D_out), .in12(Z_2_out), .in13(A_3_out), .in14(D_2_out),
    .in15(E_2_out), .out(priority_encoder_1_out));  // open: gs, en_out, en_in
  and t_prime_y_z (t_prime_y_z_out, not_1_out, y_z_out);
  and xz_prime (xz_prime_out, priority_encoder_1_out[3], not_2_out);
  not not_1 (not_1_out, priority_encoder_1_out[0]);
  not not_2 (not_2_out, priority_encoder_1_out[1]);
  not not_3 (not_3_out, priority_encoder_1_out[0]);
  and yt_prime (yt_prime_out, priority_encoder_1_out[2], not_3_out);
  and xz (xz_out, priority_encoder_1_out[3], priority_encoder_1_out[1]);
  xor y_z (y_z_out, priority_encoder_1_out[2], priority_encoder_1_out[1]);
  and xyt (xyt_out, priority_encoder_1_out[3], priority_encoder_1_out[2], priority_encoder_1_out[0]);
  or d_3 (d_3_out, xz_out, yt_prime_out);
  and x_prime_yz (x_prime_yz_out, not_4_out, priority_encoder_1_out[2], priority_encoder_1_out[1]);
  not not_4 (not_4_out, priority_encoder_1_out[3]);
  xor y_t (y_t_out, priority_encoder_1_out[2], priority_encoder_1_out[0]);
  or a_4 (a_4_out, xz_prime_out, t_prime_y_z_out, xyt_out, x_prime_yz_out, x_prime_zt_prime_out);
  and x_prime_zt_prime (x_prime_zt_prime_out, not_6_out, priority_encoder_1_out[1], not_5_out);
  not not_5 (not_5_out, priority_encoder_1_out[0]);
  not not_6 (not_6_out, priority_encoder_1_out[3]);
  or e_3 (e_3_out, y_t_out, priority_encoder_1_out[1], priority_encoder_1_out[3]);
  and xy_t_prime_z_prime (xy_t_prime_z_prime_out, priority_encoder_1_out[3], priority_encoder_1_out[2], t_prime_z_prime_out);
  nand t_prime_z_prime (t_prime_z_prime_out, priority_encoder_1_out[1], priority_encoder_1_out[0]);
  not not_7 (not_7_out, priority_encoder_1_out[2]);
  xnor y_t__prime (y_t__prime_out, priority_encoder_1_out[2], priority_encoder_1_out[0]);
  and y_prime_zt_prime (y_prime_zt_prime_out, not_7_out, priority_encoder_1_out[1], not_13_out);
  and x_y_t__prime (x_y_t__prime_out, y_t__prime_out, priority_encoder_1_out[3]);
  and xy_prime_zt (xy_prime_zt_out, priority_encoder_1_out[3], not_8_out, priority_encoder_1_out[1], priority_encoder_1_out[0]);
  and xz_prime_t_prime (xz_prime_t_prime_out, priority_encoder_1_out[3], not_9_out, not_10_out);
  not not_8 (not_8_out, priority_encoder_1_out[2]);
  not not_9 (not_9_out, priority_encoder_1_out[0]);
  not not_10 (not_10_out, priority_encoder_1_out[1]);
  not not_11 (not_11_out, priority_encoder_1_out[1]);
  not not_12 (not_12_out, priority_encoder_1_out[3]);
  not not_13 (not_13_out, priority_encoder_1_out[0]);
  and x_prime_yz_prime_t_prime (x_prime_yz_prime_t_prime_out, not_13_out, not_12_out, priority_encoder_1_out[2], not_11_out);
  or b (b_out, x_prime_zt_prime_out, xy_t_prime_z_prime_out, xz_prime_t_prime_out, xy_prime_zt_out);
  or f (f_out, x_prime_yz_prime_t_prime_out, y_prime_zt_prime_out, x_y_t__prime_out);
  and z_prime_x_y (z_prime_x_y_out, not_14_out, x_y_out);
  not not_14 (not_14_out, priority_encoder_1_out[1]);
  xor x_y (x_y_out, priority_encoder_1_out[3], priority_encoder_1_out[2]);
  and t_x_y (t_x_y_out, x_y_out, priority_encoder_1_out[0]);
  not not_15 (not_15_out, priority_encoder_1_out[0]);
  not not_16 (not_16_out, priority_encoder_1_out[2]);
  and y_prime_t (y_prime_t_out, not_16_out, priority_encoder_1_out[0]);
  and zt_prime_x_y__prime (zt_prime_x_y__prime_out, not_15_out, priority_encoder_1_out[1], x_y__prime_out);
  xnor x_y__prime (x_y__prime_out, priority_encoder_1_out[3], priority_encoder_1_out[2]);
  not not_17 (not_17_out, priority_encoder_1_out[1]);
  or g_2 (g_2_out, y_prime_t_out, priority_encoder_1_out[1], priority_encoder_1_out[3]);
  and z_prime_t (z_prime_t_out, not_17_out, priority_encoder_1_out[0]);
  or c (c_out, z_prime_x_y_out, t_x_y_out, zt_prime_x_y__prime_out, z_prime_t_out);
  _7_Segment_Display u_7_segment_display_1 (
    .g(g_2_out), .f(f_out), .a(a_4_out), .b(b_out), .e(e_3_out), .d(d_3_out), .c(c_out));  // open: dp

  // Notes on the sheet:
  //   x
  //   y
  //   z
  //   t
endmodule
